# Fritzing sketch MC38 (saved by Fritzing 0.9.3b)
breadboards: 1

parts:
  U1 = ESP32S-HiLetgo [part_number=ESP32S-HiLetgo]
  S1 = MC-38

nets:
  N1: U1.GPIO15, S1.pin_1, S1.pin_2

custom parts:
  ESP32S-HiLetgo: HiLetgo ESP-WROOM-32 ESP32 ESP-32S Development Board 2.4GHz Dual-Mode WiFi + Bluetooth Dual Cores Microcontroller The ESP32 integrated with Antenna switches, RF Balun, power amplifiers, low-noise amplifiers, filters, and management modules, and the entire solution occupies the least area of PCB. 2.4 GHz Wi-Fi plus Bluetooth dual-mode chip, with TSMC Ultra-low power consumption 40nm technology,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
  MC-38: MC-38 Contact Sensor w/ Reed Switch

// code stored in the sketch: MC38.ino
/* Created by :
symask.blogspot.com */

int state = 0;

void setup() {
  Serial.begin(9600);
  pinMode(2, INPUT_PULLUP);
  pinMode(13, OUTPUT);
}

void loop() {
  int bacaSensor = digitalRead(2);
  if (bacaSensor == HIGH && state == 0) {
    Serial.println("Pintu ada yang buka!");
    digitalWrite(13, HIGH);
    state = 1;
  }
  else if (bacaSensor == LOW) {
    state = 0;
    Serial.println("Pintu tertutup.");
    digitalWrite(13, LOW);
  }
  delay(1000);
}
