# Fritzing sketch TECLADO NUMERICO Y LCD (saved by Fritzing 0.9.3b)

parts:
  U1 = ESP32S-HiLetgo [part_number=ESP32S-HiLetgo]
  Matrix_keypad1 = KEYPAD 4x4
  Grove1 = Grove 4 Digit Display

nets:
  N1: U1.GPIO13, Grove1.CLK
  N2: U1.GPIO9, Grove1.DIO
  N3: U1.GPIO10, Grove1.GND
  N4: U1.GPIO11, Grove1.VCC
  N5: U1.GPIO0, Matrix_keypad1.col1
  N6: U1.GPIO16, Matrix_keypad1.col2
  N7: U1.GPIO17, Matrix_keypad1.row4
  N8: U1.GPIO5, Matrix_keypad1.row3
  N9: U1.GPIO18, Matrix_keypad1.row2
  N10: U1.GPIO19, Matrix_keypad1.row1
  N11: U1.GND, Matrix_keypad1.col3
  N12: U1.GPIO21, Matrix_keypad1.col4

notes:
  GPIO36
  GPIO39
  GPIO34
  GPIO32
  GPIO33
  GPIO25
  GPIO26
  GPIO27
  GPIO14
  GPIO12
  GPIO13
  GPIO9
  GPIO10
  GPIO11
  GND
  VIN
  3V3
  GPIO6
  GPIO7
  GPIO8
  GPIO0
  GPIO15
  GPIO2
  GPIO4
  GPIO16
  GPIO17
  GPIO5
  GPIO18
  GPIO19
  GPIO21
  GPIO3
  GPIO22
  EN
  GPIO23
  GPIO35
  GPIO01

custom parts:
  ESP32S-HiLetgo: HiLetgo ESP-WROOM-32 ESP32 ESP-32S Development Board 2.4GHz Dual-Mode WiFi + Bluetooth Dual Cores Microcontroller The ESP32 integrated with Antenna switches, RF Balun, power amplifiers, low-noise amplifiers, filters, and management modules, and the entire solution occupies the least area of PCB. 2.4 GHz Wi-Fi plus Bluetooth dual-mode chip, with TSMC Ultra-low power consumption 40nm technology,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
  KEYPAD 4x4: Matrix keypad 16 buttons, 4 rows x 4 columns
