# Fritzing sketch camara modificada (saved by Fritzing 0.9.3b)
perfboards: 1

parts:
  U2 = ESP32S-HiLetgo [part_number=ESP32S-HiLetgo]
  R1 = Resistor [tolerance=±5% power=0.25 resistance=4.7k package=THT]
  R4 = Resistor [tolerance=±5% power=0.25 resistance=4.7k package=THT]

nets:
  N1: U2.GPIO7, R1.Pin_1, R4.Pin_1
  N2: U2.GPIO21, R1.Pin_0
  N3: U2.GPIO23, R4.Pin_0

notes:
  GPIO4
  GPIO3
  VIN
  GPIO32
  GPIO9
  GPIO36
  GND
  GPIO13
  GPIO2
  GPIO6
  GPIO26
  GPIO25
  GPIO15
  GPIO12
  3V3
  GPIO18
  GPIO17
  GPIO19
  GPIO01
  GPIO0
  GPIO14
  GPIO23
  GPIO16
  EN
  GPIO33
  GPIO39
  GPIO5
  GPIO35
  GPIO10
  GPIO27
  GPIO8
  GPIO21
  GPIO11
  GPIO7
  GPIO34
  GPIO22
  VSYNC
  SIOC
  +VCC
  OV7670
  D0
  PCLK
  D7
  D5
  D3
  D1
  RESET
  SIOD
  HREF
  XCLK
  D6
  D4
  D2
  PWDN

custom parts:
  ESP32S-HiLetgo: HiLetgo ESP-WROOM-32 ESP32 ESP-32S Development Board 2.4GHz Dual-Mode WiFi + Bluetooth Dual Cores Microcontroller The ESP32 integrated with Antenna switches, RF Balun, power amplifiers, low-noise amplifiers, filters, and management modules, and the entire solution occupies the least area of PCB. 2.4 GHz Wi-Fi plus Bluetooth dual-mode chip, with TSMC Ultra-low power consumption 40nm technology,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
