# Fritzing sketch sensor_movimiento (saved by Fritzing 0.9.9b)
breadboards: 1

parts:
  U1 = ESP32S-HiLetgo [part_number=ESP32S-HiLetgo]
  PIR1 = PIR sensor
  R1 = Resistor [tolerance=±5% resistance=220 package="2512 [SMD]"]
  LED1 = smd LED [color="Red (633nm)" package="1206 [SMD]"]

nets:
  N1: U1.3.3, PIR1.VDD
  GND: U1.GND, U1.GPIO13, U1.GPIO21, PIR1.GND, R1.Pin_0, LED1.anode
  N2: U1.GPIO2, U1.GPIO0, PIR1.SIG
  N3: R1.Pin_1, LED1.cathode

custom parts:
  ESP32S-HiLetgo: HiLetgo ESP-WROOM-32 ESP32 ESP-32S Development Board 2.4GHz Dual-Mode WiFi + Bluetooth Dual Cores Microcontroller The ESP32 integrated with Antenna switches, RF Balun, power amplifiers, low-noise amplifiers, filters, and management modules, and the entire solution occupies the least area of PCB. 2.4 GHz Wi-Fi plus Bluetooth dual-mode chip, with TSMC Ultra-low power consumption 40nm technology,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

// code stored in the sketch: sensor_movimiento.fzz.ino
const int LEDPin= 13;
const int PIRPin= 2;

void setup()
{
  pinMode(LEDPin, OUTPUT);
  pinMode(PIRPin, INPUT);
}

void loop()
{
  int value= digitalRead(PIRPin);
 
  if (value == HIGH)
  {
    digitalWrite(LEDPin, HIGH);
    delay(50);
    digitalWrite(LEDPin, LOW);
    delay(50);
  }
  else
  {
    digitalWrite(LEDPin, LOW);
  }
}
