# Fritzing sketch sensor_presion (saved by Fritzing 0.9.9b)
circuit board: 8.46667cm x 5.64444cm
breadboards: 1

parts:
  U1 = ESP32S-HiLetgo [part_number=ESP32S-HiLetgo]
  R2 = Resistor [tolerance=±5% resistance=220 package="2512 [SMD]"]
  LED1 = LED - 5mm [color="Red (633nm)" current=0.030 package="5 mm [THT]"]
  J1 = Basic Force Sensing Resistor (FSR) [package=THT]
  R3 = Resistor [tolerance=±5% resistance=10k package="2512 [SMD]"]

nets:
  N1: U1.GPIO33, LED1.cathode
  N2: U1.GPIO12, U1.GPIO11, R2.Pin_1, J1.pin_0, J1.pin_1, R3.Pin_0, R3.Pin_1
  N3: R2.Pin_0, LED1.anode

notes:
  GPIO36
  GPIO39
  GPIO34
  GPIO32
  GPIO33
  GPIO25
  GPIO26
  GPIO27
  GPIO14
  GPIO12
  GPIO13
  GPIO9
  GPIO10
  GPIO11
  GND
  VIN
  3V3
  GPIO6
  GPIO7
  GPIO8
  GPIO0
  GPIO15
  GPIO2
  GPIO4
  GPIO16
  GPIO17
  GPIO5
  GPIO18
  GPIO19
  GPIO21
  GPIO3
  GPIO22
  EN
  GPIO23
  GPIO35
  GPIO01

custom parts:
  ESP32S-HiLetgo: HiLetgo ESP-WROOM-32 ESP32 ESP-32S Development Board 2.4GHz Dual-Mode WiFi + Bluetooth Dual Cores Microcontroller The ESP32 integrated with Antenna switches, RF Balun, power amplifiers, low-noise amplifiers, filters, and management modules, and the entire solution occupies the least area of PCB. 2.4 GHz Wi-Fi plus Bluetooth dual-mode chip, with TSMC Ultra-low power consumption 40nm technology,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

// code stored in the sketch: sensor de presion.ino
int AnalogPin = 12; //Sensor concetado a analog 0
int LEDpin = 33; // LED conectado a Pin 6 (PWN)
int ResRead; // La lectura de la resistencia por division de tension
int BrilloLED;

void setup()
{
Serial.begin(9600); // Enviaremos la informacion de depuracion a traves ddel monitor del serial
pinMode(LEDpin, OUTPUT);
}

void loop()
{Resread = analogRead(AnalogPin); // La resistencia es igual a la lectura del  senso Analog 0
Serial.print("Lectura Analogica =");
Serial.println(ResRead);

BrilloLED = map(ResRead, 0, 1023, 0, 255);
//Cambiar el rango de la lectura analogica (0-1023)
// Utilizamos en analogWrite 8 bits (0 -255) congiuramos en el map
analogWrite(LEDpin, BrilloLED);

delay(100); // Cien "ms" de espera en cada lectura
}
