# Fritzing sketch tsl-2561_dht-22 (saved by Fritzing 0.9.9b)
perfboards: 1

parts:
  U4 = ESP32S-HiLetgo [part_number=ESP32S-HiLetgo]
  RHT3 = Humidity and Temperature Sensor RHT03 [part_number=DHT22]
  R1 = Resistor [tolerance=±5% resistance=10k package="0805 [SMD]"]

nets:
  N1: U4.GND, RHT3.GND_2
  N2: U4.VIN, R1.Pin_1
  N3: U4.GPIO4, RHT3.Data-signal, R1.Pin_0

notes:
  GPIO35
  TXD
  GPIO23
  TSL2561
  EN
  GPIO22
  RXD
  GPIO21
  GND
  GPIO18
  GPIO19
  GPIO5
  GPIO17
  GPIO16
  GPIO4
  GPIO0
  GPIO2
  GPIO15
  SD1
  SD0
  CLK
  V5
  CMD
  S03
  S02
  G13
  GPIO12
  GPIO14
  GPIO27
  GPIO26
  GPIO25
  GPIO33
  GPIO32
  GPIO34
  SN
  3V
  SCL
  SDA
  IN
  SP
  3V3

custom parts:
  ESP32S-HiLetgo: HiLetgo ESP-WROOM-32 ESP32 ESP-32S Development Board 2.4GHz Dual-Mode WiFi + Bluetooth Dual Cores Microcontroller The ESP32 integrated with Antenna switches, RF Balun, power amplifiers, low-noise amplifiers, filters, and management modules, and the entire solution occupies the least area of PCB. 2.4 GHz Wi-Fi plus Bluetooth dual-mode chip, with TSMC Ultra-low power consumption 40nm technology,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
