# Fritzing sketch dht-22 (saved by Fritzing 0.9.9b)

parts:
  U2 = ESP32S-HiLetgo [part_number=ESP32S-HiLetgo]
  RHT2 = Humidity and Temperature Sensor RHT03 [part_number=DHT22]

nets:
  N1: U2.GPIO10, RHT2.GND_2
  N2: U2.GPIO7, RHT2.Vcc
  N3: U2.GPIO17, RHT2.Data-signal

notes:
  GPIO01
  GPIO35
  GPIO23
  EN
  GPIO22
  GPIO3
  GPIO21
  GPIO19
  GPIO18
  GPIO5
  GPIO17
  GPIO16
  GPIO4
  GPIO2
  GPIO15
  GPIO0
  GPIO8
  GPIO7
  GPIO6
  3V3
  VIN
  GND
  GPIO11
  GPIO10
  GPIO9
  GPIO13
  GPIO12
  GPIO14
  GPIO27
  GPIO26
  GPIO25
  GPIO33
  GPIO32
  GPIO34
  GPIO39
  GPIO36

custom parts:
  ESP32S-HiLetgo: HiLetgo ESP-WROOM-32 ESP32 ESP-32S Development Board 2.4GHz Dual-Mode WiFi + Bluetooth Dual Cores Microcontroller The ESP32 integrated with Antenna switches, RF Balun, power amplifiers, low-noise amplifiers, filters, and management modules, and the entire solution occupies the least area of PCB. 2.4 GHz Wi-Fi plus Bluetooth dual-mode chip, with TSMC Ultra-low power consumption 40nm technology,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
